# Fritzing sketch plataformafinal (saved by Fritzing 0.9.3b)
breadboards: 2

parts:
  Componente1 = Arduino Mega 2560 (Rev3)
  Componente2 = Ambient Light Sensor (TEMT6000 Breakout Board)
  U1 = LM358 [package=dip08]
  R3 = Resistor [tolerance=±5% resistance=1k package=THT]
  R4 = Resistor [tolerance=±5% resistance=1k package=THT]
  Componente3 = Arduino Nano (Rev3.0)
  LED4 = smd LED [color="White (4500K)" package="0603 [SMD]"]
  LED5 = smd LED [color="White (4500K)" package="0603 [SMD]"]
  LED6 = smd LED [color="White (4500K)" package="0603 [SMD]"]
  LED7 = smd LED [color="White (4500K)" package="0603 [SMD]"]
  R5 = Resistor [tolerance=±2% resistance=330 package="0603 [SMD]"]

nets:
  5V: Componente1.5V, Componente2.VCC, U1.G$1_V+, R4.Pin_1
  GND: Componente1.GND, Componente2.GND, U1.G$1_V-, R3.Pin_1
  N1: Componente1.D2_PWM, U1.G$1_OUT
  N2: Componente2.S, U1.G$1_+IN
  N3: U1.G$1_-IN, R3.Pin_0, R4.Pin_0
  N4: Componente3.GND, LED4.cathode, LED5.cathode, LED6.cathode, LED7.cathode
  N5: Componente3.D2, R5.Pin_1
  N6: LED4.anode, LED5.anode, LED6.anode, LED7.anode, R5.Pin_0
