# Fritzing sketch receptor (saved by Fritzing 0.9.3b)
breadboards: 1

parts:
  U1 = LM358 [package=dip08]
  Componente1 = Arduino Mega 2560 (Rev3)
  part = Resistor [tolerance=±5% resistance=1k package=THT]
  part_2 = Resistor [tolerance=±5% resistance=100k package=THT]
  Componente2 = Ambient Light Sensor (TEMT6000 Breakout Board)
  R2 = Resistor [tolerance=±5% resistance=100k package=THT]

nets:
  N1: U1.G$1_OUT, Componente1.D2_PWM
  N2: U1.G$1_-IN, part.Pin_0, part_2.Pin_0, R2.Pin_0
  N3: U1.G$1_+IN, Componente2.S
  GND: U1.G$1_V-, Componente1.GND, part.Pin_1, Componente2.GND
  5V: U1.G$1_V+, Componente1.5V, part_2.Pin_1, Componente2.VCC, R2.Pin_1
