# Fritzing sketch transmissor (saved by Fritzing 0.9.3b)
breadboards: 1

parts:
  Componente2 = Arduino Nano (Rev3.0)
  R1 = Resistor [tolerance=±2% resistance=330 package="0603 [SMD]"]
  LED3 = smd LED [color="White (4500K)" package="0603 [SMD]"]
  LED3_2 = smd LED [color="White (4500K)" package="0603 [SMD]"]
  LED3_3 = smd LED [color="White (4500K)" package="0603 [SMD]"]
  LED3_4 = smd LED [color="White (4500K)" package="0603 [SMD]"]

nets:
  N1: Componente2.GND, LED3.cathode, LED3_2.cathode, LED3_3.cathode, LED3_4.cathode
  N2: Componente2.D2, R1.Pin_1
  N3: R1.Pin_0, LED3.anode, LED3_2.anode, LED3_3.anode, LED3_4.anode
